# Fritzing sketch Ambient_BatteryCheck (saved by Fritzing 0.9.3b)
circuit board: 8.46667cm x 5.64444cm
breadboards: 1

parts:
  U1 = ESP-WROOM-02-AE [part_number=ESP-WROOM-02-AE]
  R1 = Resistor [tolerance=±5% resistance=10k package=THT]
  S1 = Pushbutton [package="[THT]"]
  R2 = Resistor [tolerance=±5% resistance=47 package=THT]
  LED1 = LED - 5mm [color="Red (633nm)" package="5 mm [THT]"]
  R3 = Resistor [tolerance=±5% resistance=10k package=THT]
  VCC1 = Battery
  パーツ1 = Arduino Pro Mini (3.3V)
  BAT1 = BATTERY-2 [package=battery-aaa]
  BAT2 = BATTERY-2 [package=battery-aaa]

nets:
  N1: U1.3V3, R1.Pin_1, R3.Pin_0, VCC1.+
  N2: U1.EN, R3.Pin_1
  N3: U1.GND, S1.Pin_1, S1.Pin_2, R2.Pin_0, VCC1.-, BAT1.-1, BAT2.-1
  N4: U1.IO16, LED1.anode
  N5: U1.RST, R1.Pin_0, S1.Pin_3, S1.Pin_4
  N6: U1.IO5, パーツ1.A5
  N7: U1.IO4, パーツ1.A4
  N8: R2.Pin_1, LED1.cathode
  N9: パーツ1.A1, BAT2.+1
  N10: パーツ1.A0, BAT1.+1

custom parts:
  ESP-WROOM-02-AE: ESP-WROOM-02 with the DIP breakout board by Akizuki-Electronics in Japan. See http://akizukidenshi.com/catalog/g/gK-09758/ for the detauls.
